# Fritzing sketch assembly (saved by Fritzing 0.9.3b)
breadboards: 2

parts:
  U1 = RF-LINK_TX [package=rf-link_tx]
  U4 = HT8950 [package=dil18]
  Q1 = NPN-Transistor [package="TO92 [THT]"]
  R1 = Resistor [tolerance=±5% resistance=750k package=THT]
  VCC1 = Battery block 9V
  J1 = Piezo Speaker
  S1 = Momentary Switch [package=ksa_sealed_tac_switch]
  U6 = HT8950 [package=dil18]
  ULN2 = Darlington Driver [package=dil18]
  Q3 = NPN-Transistor [package="TO92 [THT]"]
  R3 = Resistor [tolerance=±5% resistance=33k package=THT]
  Maluska2 = maluska dil miniaturrelais [part_number="DIL Mini RY" package=THT]
  VCC4 = Battery block 9V
  VCC5 = Battery block 9V
  U7 = RF-LINK_RX [package=rf-link_rx]
  U8 = Vibration Motor- ROB-08449 [package=vibe-motor-10mm]

nets:
  N1: U1.DATA, U4.LAMP
  N2: U1.GND, U4.AO, U4.ROB, Q1.B, VCC1.-, S1.3
  N3: U1.+5V, U4.AUDIO, Q1.C, J1.pin1
  N4: U4.VSS, J1.pin2, S1.2
  N5: U4.AIN, R1.Pin_1
  N6: U4.VDD, R1.Pin_0
  N7: Q1.E, VCC1.+
  N8: U6.OSC2, ULN2.1
  N9: U6.VIB, R3.Pin_0
  N10: U6.TGU, R3.Pin_1
  N11: U6.ROB, ULN2.10, Q3.C, U7.GND
  N12: ULN2.9, Q3.B, Maluska2.4, VCC4.-, VCC5.-, U7.DATA, U7.ANT, U8.+
  N13: ULN2.18, Maluska2.1
  N14: Q3.E, VCC4.+
  N15: Maluska2.6, U8.-
  N16: Maluska2.16, VCC5.+
